// Digital circuit alu.dig as structural Verilog
module alu (
  input  [31:0] A,
  input  [31:0] B,
  input  [3:0] ALUOperation,
  output FlagZ,
  output [31:0] Result
);

  wire add_sub_1_overflow, add_sub_1_sign, is__slt_eq, is__sub_eq, or_1_out;
  wire [0:0] comp_out_ext;
  wire [31:0] add_sub_out, boolean_out;

  Comparator #(.Bits(4)) is__sub (.a(ALUOperation), .b(4'b0110), .eq(is__sub_eq));  // open: gt, lt
  Comparator #(.Bits(4)) is__slt (.a(ALUOperation), .b(4'b0111), .eq(is__slt_eq));  // open: gt, lt
  or or_1 (or_1_out, is__sub_eq, is__slt_eq);
  boolean_unit boolean_unit_1 (.A(A), .B(B), .Bool(ALUOperation[1:0]), .Out(boolean_out));
  add_sub add_sub_1 (
    .B(B), .A(A), .Sub(or_1_out), .Out(add_sub_out), .Overflow(add_sub_1_overflow), .Sign(add_sub_1_sign));
  comparator comparator_1 (.Sign(add_sub_1_sign), .Overflow(add_sub_1_overflow), .Result(comp_out_ext[0]));
  Multiplexer #(.Selector_Bits(2), .Bits(32)) multiplexer_1 (
    .sel(ALUOperation[1:0]), .in_0(boolean_out), .in_1(boolean_out), .in_2(add_sub_out),
    .in_3({{31{1'b0}}, comp_out_ext[0]}), .out(Result));
  Comparator #(.Bits(32)) comparator_2 (.a(Result), .b({32{1'b0}}), .eq(FlagZ));  // open: gt, lt

  // Notes on the sheet:
  //   Control Bits
  //   Inputs
  //   Outputs
endmodule

/* Test case ALU Test:
A B ALUOperation Result

# ADD tests (ALUOperation = 0010)
0x289322C4 0x01846399 0b0010 0x2A17865D
0x4152A22D 0x22042121 0b0010 0x6356C34E
0x84893212 0x0994AD1A 0b0010 0x8E1DDF2C
0x90A8826C 0x112109FB 0b0010 0xA1C98C67
0x5210C12D 0x3D04ABBC 0b0010 0x8F156CE9
0x90D194B5 0xB005500E 0b0010 0x40D6E4C3

# SUB tests (ALUOperation = 0110)
0x39332544 0x0435FCAD 0b0110 0x34FD2897
0x59286AB1 0x221FB76C 0b0110 0x3708B345
0xECD55935 0x248C5A4B 0b0110 0xC848FEEA
0x902A9525 0xE5454D48 0b0110 0xAAE547DD
0x8211036A 0x7B13890A 0b0110 0x06FD7A60
0x5FE15DBE 0x8934B9B1 0b0110 0xD6ACA40D

# AND tests (ALUOperation = 0000)
0xdcd84709 0x768a5af3 0b0000 0x54884201
0x3d2cd361 0xf53106ef 0b0000 0x35200261
0x28f56e63 0x854b7d0b 0b0000 0x00416C03

# OR tests (ALUOperation = 0001)
0x0f9eda3f 0x885e0a47 0b0001 0x8FDEDA7F
0xca58eed8 0x514af1fa 0b0001 0xDB5AFFFA
0xc7100004 0x3553ef1e 0b0001 0xF753EF1E

# SLT tests (ALUOperation = 0111), signed A < B ? 1 : 0
0x289322C4 0x01846399 0b0111 0x00000000   # both positive, A > B
0x4152A22D 0x22042121 0b0111 0x00000000   # both positive, A > B
0x84893212 0x0994AD1A 0b0111 0x00000001   # A negative, B positive
0x90A8826C 0x112109FB 0b0111 0x00000001   # A negative, B positive
0x5210C12D 0x3D04ABBC 0b0111 0x00000000   # both positive, A > B
0x90D194B5 0xB005500E 0b0111 0x00000001   # both negative, A < B
*/
