// Digital circuit control-unit.dig as structural Verilog
module control_unit (
  input  [6:0] opcode,
  input  [2:0] funct3,
  input  [6:0] funct7,
  output ALUOp0,
  output ALUOp1,
  output ALUOp2,
  output ALUOp3,
  output ImmSrc0,
  output ImmSrc1,
  output ALUSrc,
  output RegWrite
);

  wire and_1_out, and_2_out, and_3_out, and_4_out, and_5_out, and_6_out, and_7_out, and_8_out, f30, f32, f36,
       f37, f70, f720, op13, op33;
  wire [2:0] priorityencoder_1_num;

  Comparator #(.Bits(7)) comparator_1 (.a(opcode), .b(7'b0110011), .eq(op33));  // open: gt, lt
  Comparator #(.Bits(7)) comparator_2 (.a(opcode), .b(7'b0010011), .eq(op13));  // open: gt, lt
  Comparator #(.Bits(3)) comparator_3 (.a(funct3), .b(3'b000), .eq(f30));  // open: gt, lt
  Comparator #(.Bits(3)) comparator_4 (.a(funct3), .b(3'b010), .eq(f32));  // open: gt, lt
  Comparator #(.Bits(3)) comparator_5 (.a(funct3), .b(3'b111), .eq(f37));  // open: gt, lt
  Comparator #(.Bits(3)) comparator_6 (.a(funct3), .b(3'b110), .eq(f36));  // open: gt, lt
  Comparator #(.Bits(7)) comparator_7 (.a(funct7), .b({7{1'b0}}), .eq(f70));  // open: gt, lt
  Comparator #(.Bits(7)) comparator_8 (.a(funct7), .b(7'b0100000), .eq(f720));  // open: gt, lt
  and and_1 (and_1_out, op33, f30, f70);
  and and_2 (and_2_out, op33, f30, f720);
  and and_3 (and_3_out, op33, f37, f70);
  and and_4 (and_4_out, op33, f36, f70);
  and and_5 (and_5_out, op33, f32, f70);
  and and_6 (and_6_out, op13, f30);
  and and_7 (and_7_out, op13, f32);
  and and_8 (and_8_out, op13, f37);
  PriorityEncoder #(.Selector_Bits(3)) priorityencoder_1 (
    .in0(and_1_out), .in1(and_2_out), .in2(and_3_out), .in3(and_4_out), .in4(and_5_out), .in5(and_6_out),
    .in6(and_7_out), .in7(and_8_out), .num(priorityencoder_1_num));  // open: any
  ROM #(.AddrBits(3), .Bits(8)) rom_1 (
    .A(priorityencoder_1_num), .sel(1'b1),
    .D({RegWrite, ALUSrc, ImmSrc1, ImmSrc0, ALUOp3, ALUOp2, ALUOp1, ALUOp0}));

  // Notes on the sheet:
  //   contents of rom_1 (hex, n*v repeats v):
  //   82,86,80,81,87,c2,c7,c0
endmodule

/* Test case Control Unit:
opcode   funct3  funct7    RegWrite ALUSrc ImmSrc1 ImmSrc0 ALUOp3 ALUOp2 ALUOp1 ALUOp0
0b0110011 0b000  0b0000000 0b1      0b0    0b0     0b0     0b0    0b0    0b1    0b0
0b0110011 0b000 0b0100000 0b1 0b0 0b0 0b0 0b0 0b1 0b1 0b0
0b0110011 0b111 0b0000000 0b1 0b0 0b0 0b0 0b0 0b0 0b0 0b0
0b0110011 0b110 0b0000000 0b1 0b0 0b0 0b0 0b0 0b0 0b0 0b1
0b0110011 0b010 0b0000000 0b1 0b0 0b0 0b0 0b0 0b1 0b1 0b1
0b0010011 0b000 0b0000000 0b1 0b1 0b0 0b0 0b0 0b0 0b1 0b0
0b0010011 0b010 0b0000000 0b1 0b1 0b0 0b0 0b0 0b1 0b1 0b1
0b0010011 0b111 0b0000000 0b1 0b1 0b0 0b0 0b0 0b0 0b0 0b0
*/
