// Digital circuit cpu.dig as structural Verilog
module cpu (
  input  clk,
  output [31:0] ReadData1,
  output [31:0] ReadData2
);

  wire ALUOp0, ALUOp1, ALUOp2, ALUOp3, ALUSrc, ImmSrc0, ImmSrc1, RegWrite;
  wire [2:0] funct3;
  wire [4:0] imm12, rd, rs1;
  wire [6:0] funct7, opcode;
  wire [31:0] add_1_s, alu_1_result, ALU_input_B, imm_ext, PC_q;

  Multiplexer #(.Bits(32)) multiplexer_1 (.sel(ALUSrc), .in_0(ReadData2), .in_1(imm_ext), .out(ALU_input_B));
  Register #(.Bits(32), .isProgramCounter("true")) PC (.D(add_1_s), .C(clk), .en(1'b1), .Q(PC_q));
  alu alu_1 (
    .A(ReadData1), .B(ALU_input_B), .ALUOperation({ALUOp3, ALUOp2, ALUOp1, ALUOp0}), .Result(alu_1_result));  // open: FlagZ
  Add #(.Bits(32)) add_1 (.a(32'h4), .b(PC_q), .c_i(1'b0), .s(add_1_s));  // open: c_o
  ROM #(.AddrBits(10), .isProgramMemory("true"), .Bits(32)) Instruction_Memory (
    .A(PC_q[11:2]), .sel(1'b1), .D({funct7, imm12, rs1, funct3, rd, opcode}));
  register_file register_file_1 (
    .ReadReg1(rs1), .ReadReg2(imm12), .WriteReg(rd), .WriteData(alu_1_result), .RegWrite(RegWrite),
    .Clock(clk), .ReadData1(ReadData1), .ReadData2(ReadData2));
  control_unit control_unit_1 (
    .opcode(opcode), .funct3(funct3), .funct7(funct7), .ALUOp0(ALUOp0), .ALUOp1(ALUOp1), .ALUOp2(ALUOp2),
    .ALUOp3(ALUOp3), .ImmSrc0(ImmSrc0), .ImmSrc1(ImmSrc1), .ALUSrc(ALUSrc), .RegWrite(RegWrite));
  BitExtender #(.inputBits(12), .outputBits(32)) bitextender_1 (.in({funct7, imm12}), .out(imm_ext));

  // Other names for the same wires on the sheet: rs2[4:0] = imm12; imm12[11:5] = funct7; clock = clk

  // Notes on the sheet:
  //   contents of Instruction_Memory (hex, n*v repeats v):
  //   45467830,32303043,302c3331,30463778,39323032,78302c33,32313037
  //   ,33313338,3578302c,30333133,2c333933,32317830,37373333,302c3331
  //   ,43313778,39373737,78302c33,37313435,33393846,3178302c,32323733
  //   ,d333139,3078300a,32393230,2c333939,30307830,41413930,302c3331
  //   ,44464678,39413241,78302c33,41353030,33314241,3078302c,30423030
  //   ,2c333130,45467830,42323243,302c3339,30303078,31303842,78302c33
  //   ,35364146,33314341,78300a0d,7*78302c30,300a0d30,7*302c3078,a0d3078
  //   ,7*2c307830,d307830,3078300a,7*3078302c,78300a0d,7*78302c30,a0d30
endmodule

/* Test case cpu:
clk ReadData1 ReadData2
0 0 0		# addi $4 $0 -20
C (-20) 0 	# addi $5 $4 0x7FFF
C 32747 0 	# addi $6 $5 0x7018
C 61443 0 	# addi $7 $6 0x5311
C 0 0 		# ori $10 $0 10
C 10 0 		# ori $11 $10 0xFF55
C 65375 0 	# ori $12 $11 39
C 61443 0 	# andi $14 $6 0xE123
C 57347 0 	# andi $15 $14 0xFF1C
C 57344 0 	# andi $17 $15 0x541
C (-20) 0 	# slti $18 $4 311
C 1 0 		# slti $19 $18 2
C 1 0 		# slti $20 $19 0
C 0 0 		# slti $21 $20 -3	
C 0 0 		# slti $22 $21 5 
C 1 0 		# addi $0 $22 0 
C (-20) 0 	# slti $23 $4 -20	
C 0 0 		# addi $0 $23 0
C 65375 0 	# slti $24 $11 -90 
C 0 0 		# addi $0 $24 0
C (-20) 0 	# slti $25 $4 0 
C 1 0 		# addi $0 $25 0 
C 65375 0 	# slti $26 $11 6000
C 0 0 		# addi $0 $26 0 
C (-20) 0 	# slti $27 $4 -1 
C 1 0 		# addi $0 $27 0	
*/
