// Digital circuit register-file.dig as structural Verilog
module register_file (
  input  [4:0] ReadReg1,
  input  [4:0] ReadReg2,
  input  [4:0] WriteReg,
  input  [31:0] WriteData,
  input  RegWrite,
  input  Clock,
  output [31:0] ReadData1,
  output [31:0] ReadData2
);

  wire en0, en1, en2, en3, en4, en5, en6, en7, en8, en9, en10, en11, en12, en13, en14, en15, en16, en17,
       en18, en19, en20, en21, en22, en23, en24, en25, en26, en27, en28, en29, en30, en31, wen0, wen1, wen2,
       wen3, wen4, wen5, wen6, wen7, wen8, wen9, wen10, wen11, wen12, wen13, wen14, wen15, wen16, wen17,
       wen18, wen19, wen20, wen21, wen22, wen23, wen24, wen25, wen26, wen27, wen28, wen29, wen30, wen31;
  wire [31:0] Reg0, Reg1, Reg2, Reg3, Reg4, Reg5, Reg6, Reg7, Reg8, Reg9, Reg10, Reg11, Reg12, Reg13, Reg14,
       Reg15, Reg16, Reg17, Reg18, Reg19, Reg20, Reg21, Reg22, Reg23, Reg24, Reg25, Reg26, Reg27, Reg28,
       Reg29, Reg30, Reg31;

  Register #(.Bits(32)) u_Reg0 (.D(WriteData), .C(Clock), .en(en0), .Q(Reg0));
  Register #(.Bits(32)) u_Reg1 (.D(WriteData), .C(Clock), .en(en1), .Q(Reg1));
  Register #(.Bits(32)) u_Reg2 (.D(WriteData), .C(Clock), .en(en2), .Q(Reg2));
  Register #(.Bits(32)) u_Reg3 (.D(WriteData), .C(Clock), .en(en3), .Q(Reg3));
  Register #(.Bits(32)) u_Reg4 (.D(WriteData), .C(Clock), .en(en4), .Q(Reg4));
  Register #(.Bits(32)) u_Reg5 (.D(WriteData), .C(Clock), .en(en5), .Q(Reg5));
  Register #(.Bits(32)) u_Reg6 (.D(WriteData), .C(Clock), .en(en6), .Q(Reg6));
  Register #(.Bits(32)) u_Reg7 (.D(WriteData), .C(Clock), .en(en7), .Q(Reg7));
  Register #(.Bits(32)) u_Reg8 (.D(WriteData), .C(Clock), .en(en8), .Q(Reg8));
  Register #(.Bits(32)) u_Reg9 (.D(WriteData), .C(Clock), .en(en9), .Q(Reg9));
  Register #(.Bits(32)) u_Reg10 (.D(WriteData), .C(Clock), .en(en10), .Q(Reg10));
  Register #(.Bits(32)) u_Reg11 (.D(WriteData), .C(Clock), .en(en11), .Q(Reg11));
  Register #(.Bits(32)) u_Reg12 (.D(WriteData), .C(Clock), .en(en12), .Q(Reg12));
  Register #(.Bits(32)) u_Reg13 (.D(WriteData), .C(Clock), .en(en13), .Q(Reg13));
  Register #(.Bits(32)) u_Reg14 (.D(WriteData), .C(Clock), .en(en14), .Q(Reg14));
  Register #(.Bits(32)) u_Reg15 (.D(WriteData), .C(Clock), .en(en15), .Q(Reg15));
  Register #(.Bits(32)) u_Reg16 (.D(WriteData), .C(Clock), .en(en16), .Q(Reg16));
  Register #(.Bits(32)) u_Reg17 (.D(WriteData), .C(Clock), .en(en17), .Q(Reg17));
  Register #(.Bits(32)) u_Reg18 (.D(WriteData), .C(Clock), .en(en18), .Q(Reg18));
  Register #(.Bits(32)) u_Reg19 (.D(WriteData), .C(Clock), .en(en19), .Q(Reg19));
  Register #(.Bits(32)) u_Reg20 (.D(WriteData), .C(Clock), .en(en20), .Q(Reg20));
  Register #(.Bits(32)) u_Reg21 (.D(WriteData), .C(Clock), .en(en21), .Q(Reg21));
  Register #(.Bits(32)) u_Reg22 (.D(WriteData), .C(Clock), .en(en22), .Q(Reg22));
  Register #(.Bits(32)) u_Reg23 (.D(WriteData), .C(Clock), .en(en23), .Q(Reg23));
  Register #(.Bits(32)) u_Reg24 (.D(WriteData), .C(Clock), .en(en24), .Q(Reg24));
  Register #(.Bits(32)) u_Reg25 (.D(WriteData), .C(Clock), .en(en25), .Q(Reg25));
  Register #(.Bits(32)) u_Reg26 (.D(WriteData), .C(Clock), .en(en26), .Q(Reg26));
  Register #(.Bits(32)) u_Reg27 (.D(WriteData), .C(Clock), .en(en27), .Q(Reg27));
  Register #(.Bits(32)) u_Reg28 (.D(WriteData), .C(Clock), .en(en28), .Q(Reg28));
  Register #(.Bits(32)) u_Reg29 (.D(WriteData), .C(Clock), .en(en29), .Q(Reg29));
  Register #(.Bits(32)) u_Reg30 (.D(WriteData), .C(Clock), .en(en30), .Q(Reg30));
  Register #(.Bits(32)) u_Reg31 (.D(WriteData), .C(Clock), .en(en31), .Q(Reg31));
  Multiplexer #(.Selector_Bits(5), .Bits(32)) multiplexer_1 (
    .sel(ReadReg1), .in_0(Reg0), .in_1(Reg1), .in_2(Reg2), .in_3(Reg3), .in_4(Reg4), .in_5(Reg5),
    .in_6(Reg6), .in_7(Reg7), .in_8(Reg8), .in_9(Reg9), .in_10(Reg10), .in_11(Reg11), .in_12(Reg12),
    .in_13(Reg13), .in_14(Reg14), .in_15(Reg15), .in_16(Reg16), .in_17(Reg17), .in_18(Reg18), .in_19(Reg19),
    .in_20(Reg20), .in_21(Reg21), .in_22(Reg22), .in_23(Reg23), .in_24(Reg24), .in_25(Reg25), .in_26(Reg26),
    .in_27(Reg27), .in_28(Reg28), .in_29(Reg29), .in_30(Reg30), .in_31(Reg31), .out(ReadData1));
  and and_1 (en1, wen1, RegWrite);
  and and_2 (en2, wen2, RegWrite);
  and and_3 (en3, wen3, RegWrite);
  and and_4 (en4, wen4, RegWrite);
  and and_5 (en5, wen5, RegWrite);
  and and_6 (en6, wen6, RegWrite);
  and and_7 (en7, wen7, RegWrite);
  and and_8 (en8, wen8, RegWrite);
  Multiplexer #(.Selector_Bits(5), .Bits(32)) multiplexer_2 (
    .sel(ReadReg2), .in_0(Reg0), .in_1(Reg1), .in_2(Reg2), .in_3(Reg3), .in_4(Reg4), .in_5(Reg5),
    .in_6(Reg6), .in_7(Reg7), .in_8(Reg8), .in_9(Reg9), .in_10(Reg10), .in_11(Reg11), .in_12(Reg12),
    .in_13(Reg13), .in_14(Reg14), .in_15(Reg15), .in_16(Reg16), .in_17(Reg17), .in_18(Reg18), .in_19(Reg19),
    .in_20(Reg20), .in_21(Reg21), .in_22(Reg22), .in_23(Reg23), .in_24(Reg24), .in_25(Reg25), .in_26(Reg26),
    .in_27(Reg27), .in_28(Reg28), .in_29(Reg29), .in_30(Reg30), .in_31(Reg31), .out(ReadData2));
  and and_9 (en9, wen9, RegWrite);
  and and_10 (en10, wen10, RegWrite);
  and and_11 (en11, wen11, RegWrite);
  and and_12 (en12, wen12, RegWrite);
  and and_13 (en13, wen13, RegWrite);
  and and_14 (en14, wen14, RegWrite);
  and and_15 (en15, wen15, RegWrite);
  and and_16 (en16, wen16, RegWrite);
  and and_17 (en17, wen17, RegWrite);
  and and_18 (en18, wen18, RegWrite);
  and and_19 (en19, wen19, RegWrite);
  and and_20 (en20, wen20, RegWrite);
  and and_21 (en21, wen21, RegWrite);
  and and_22 (en22, wen22, RegWrite);
  and and_23 (en23, wen23, RegWrite);
  and and_24 (en24, wen24, RegWrite);
  Decoder #(.Selector_Bits(5)) decoder_1 (
    .sel(WriteReg), .out_0(wen0), .out_1(wen1), .out_2(wen2), .out_3(wen3), .out_4(wen4), .out_5(wen5),
    .out_6(wen6), .out_7(wen7), .out_8(wen8), .out_9(wen9), .out_10(wen10), .out_11(wen11), .out_12(wen12),
    .out_13(wen13), .out_14(wen14), .out_15(wen15), .out_16(wen16), .out_17(wen17), .out_18(wen18),
    .out_19(wen19), .out_20(wen20), .out_21(wen21), .out_22(wen22), .out_23(wen23), .out_24(wen24),
    .out_25(wen25), .out_26(wen26), .out_27(wen27), .out_28(wen28), .out_29(wen29), .out_30(wen30),
    .out_31(wen31));
  and and_25 (en25, wen25, RegWrite);
  and and_26 (en26, wen26, RegWrite);
  and and_27 (en27, wen27, RegWrite);
  and and_28 (en28, wen28, RegWrite);
  and and_29 (en29, wen29, RegWrite);
  and and_30 (en30, wen30, RegWrite);
  and and_31 (en31, wen31, RegWrite);
  and and_32 (en0, wen0, 1'b0);

  // Other names for the same wires on the sheet: clk = Clock
endmodule

/* Test case Register File Test:
WriteReg WriteData RegWrite Clock ReadReg1 ReadReg2 ReadData1 ReadData2

# $1 = 25
1 25 1 C 1 0 25 0

# $2 = 30
2 30 1 C 0 2 0 30

# $(N+1) = (N+1)
loop(N, 30)
	(N+1) (N+1) 1 C (N+1) (N) (N+1) (N)
end loop

# $(N+1) = N-60
loop(N, 30)
	(N+1) (N-60) 1 C (N+1) (N+1) (N-60) (N-60)
end loop

# Try writing to $0. This should not write anything
0 25 1 C 0 0 0 0

# try writing when RegWrite = 0
# (the registers should still have their old values)
loop(N, 30)
	(N+1) (N+80) 0 C (N+1) (N+1) (N-60) (N-60)
end loop
*/
